# Fritzing sketch schematic (saved by Fritzing 0.9.2b)
circuit board: 5.40842cm x 5.26023cm
breadboards: 1

parts:
  Nano1 = Arduino Nano v2.3
  J1 = Screw terminal - 2 pins [package=THT]
  J2 = male pin header, 3 pins [form="♂ (male)"]
  J3 = female pin header, 5 pins [form="♀ (female)"]
  J4 = female pin header, 5 pins [form="♀ (female)"]
  LED1 = LED - 3mm [color="Red (633nm)" package="3 mm [THT]"]
  LED2 = LED - 3mm [color="Green (570nm)" package="3 mm [THT]"]
  R3 = Resistor [tolerance=±5% resistance=220 package=THT]
  R2 = Resistor [tolerance=±0.05% resistance=220 package=THT]

nets:
  N1: Nano1.GND, J1.pin1, J2.pin3, J3.pin1, LED1.cathode, LED2.cathode
  N2: Nano1.D2, J3.pin5
  N3: Nano1.D3, J2.pin2
  N4: Nano1.D5, R3.Pin_1
  N5: Nano1.D6, R2.Pin_1
  N6: Nano1.D10, J4.pin2
  N7: Nano1.D11, J4.pin3
  N8: Nano1.D12, J3.pin4
  N9: Nano1.D13, J3.pin3
  N10: Nano1.+5V, J2.pin1, J4.pin1
  N11: Nano1.VIN, J1.pin2
  N12: LED1.anode, R2.Pin_0
  N13: LED2.anode, R3.Pin_0
